// Digital circuit bomba.dig as structural Verilog
module bomba (
  input  encendido,
  input  minimo,
  input  cebado,
  output Bombeando
);

  wire and_1_out, and_2_out, descebada_q;

  and and_1 (and_1_out, encendido, ~minimo);  // And
  and and_2 (and_2_out, minimo, cebado);
  RS_FF_AS descebada (.S(and_1_out), .R(and_2_out), .Q(descebada_q));  // open: nQ
  and and_3 (Bombeando, encendido, ~descebada_q);  // And
endmodule
