// Digital circuit control_bomba.dig as structural Verilog
module control_bomba (
  input  tanqueH,
  input  tanqueL,
  input  cisternaOK,
  input  cisternaL,
  output bomba
);

  wire and_1_out, and_2_out, nand_1_out, or_1_out;

  nand nand_1 (nand_1_out, tanqueH, tanqueL);
  and and_1 (and_1_out, cisternaOK, cisternaL);
  and and_2 (and_2_out, nand_1_out, and_1_out);
  or or_1 (or_1_out, tanqueH, nand_1_out);
  D_FF_AS d_ff_as_1 (.Set(and_2_out), .D(and_2_out), .C(and_2_out), .Clr(or_1_out), .Q(bomba));  // open: nQ
endmodule
