// Digital circuit sim_unidad_aritmetico_logica.dig as structural Verilog
module sim_unidad_aritmetico_logica (
  input  [15:0] A,
  input  [15:0] B,
  output [15:0] Resultado
);

  wire and_out, logica_out, resta_out;

  DipSwitch resta (.out(resta_out));
  DipSwitch logica (.out(logica_out));
  DipSwitch \and  (.out(and_out));
  unidad_aritmetico_logica unidad_aritmetico_logica_1 (
    .A(A), .B(B), .invB(resta_out), .R(Resultado), .logica(logica_out), .\and (and_out));

  // Notes on the sheet:
  //   A: Primer Operando
  //   B: Segundo Operando
  //   Resultado: resta | logica | and | resultado
  //     0          0       x        (A + B)
  //     1          0       x        (A - B)
  //     0          1       0        (A or B)
  //     1          1       0        (A or not B)
  //     0          1       1        (A and B)
  //     1          1       1        (A and not B)
endmodule
