// Digital circuit tanque.dig as structural Verilog
module tanque (
  input  carga,
  input  descarga,
  input  ck,
  output [9:0] Nivel
);

  wire priorityencoder_1_any, priorityencoder_1_num;
  wire [9:0] multiplexer_1_out, multiplexer_2_out;

  PriorityEncoder priorityencoder_1 (
    .in0(descarga), .in1(carga), .num(priorityencoder_1_num), .any(priorityencoder_1_any));
  Multiplexer #(.Bits(10), .generic("this.Bits=args.bits;")) multiplexer_1 (
    .sel(priorityencoder_1_num), .in_0({1'b0, Nivel[9:1]}), .in_1({Nivel[8:0], 1'b1}), .out(multiplexer_1_out));
  Multiplexer #(.generic("this.Bits=args.bits;")) multiplexer_2 (
    .sel(priorityencoder_1_any), .in_0(Nivel), .in_1(multiplexer_1_out), .out(multiplexer_2_out));
  D_FF #(.Bits(10), .generic("this.Bits=args.bits;")) d_ff_1 (.D(multiplexer_2_out), .C(ck), .Q(Nivel));  // open: nQ

  // Notes on the sheet:
  //   Ver
  //   https://github.com/hneemann/Digital/discussions/860#discussioncomment-1516485
endmodule

/* Code that sets the parameters or builds the circuit:
bits:=4;
*/
