// Digital circuit unidad_aritmetica_logica.dig as structural Verilog
module unidad_aritmetica_logica (
  input  [15:0] A,
  input  [15:0] B,
  input  invB,
  input  logica,
  input  \and ,
  output [15:0] R
);

  wire [15:0] add_1_s, add_2_s, and_1_out, and_2_out, nor_1_out, not_1_out, not_2_out, not_3_out, or_1_out;

  Add #(.Bits(16)) add_1 (.a(A), .b(B), .c_i(1'b0), .s(add_1_s));  // open: c_o
  assign or_1_out = A | B;  // Or or_1, 16 bits wide
  assign and_1_out = A & B;  // And and_1, 16 bits wide
  Add #(.Bits(16)) add_2 (.a(A), .b(not_1_out), .c_i(1'b1), .s(add_2_s));  // open: c_o
  assign not_1_out = ~B;  // Not not_1, 16 bits wide
  assign nor_1_out = ~(not_2_out | B);  // NOr nor_1, 16 bits wide
  assign not_2_out = ~A;  // Not not_2, 16 bits wide
  assign and_2_out = A & not_3_out;  // And and_2, 16 bits wide
  assign not_3_out = ~B;  // Not not_3, 16 bits wide
  Multiplexer #(.Selector_Bits(3), .Bits(16)) multiplexer_1 (
    .sel({invB, logica, \and }), .in_0(add_1_s), .in_1(add_1_s), .in_2(or_1_out), .in_3(and_1_out),
    .in_4(add_2_s), .in_5(add_2_s), .in_6(nor_1_out), .in_7(and_2_out), .out(R));
endmodule
